# Fritzing sketch watering-esp8266 (saved by Fritzing 0.9.2b)
breadboards: 1

parts:
  U1 = ESP8266 WiFi Module [part_number=ESP8266]
  LED1 = LED - 5mm [color="Red (633nm)" package="5 mm [THT]"]
  S2 = Pushbutton [package="[SMD]"]
  S1 = Pushbutton [package="[SMD]"]
  IC1 = Voltage Regulator [package=to-220-alt]
  U2 = 4-Channel 5v Relay Shield [package=relay-4ch5v10a]
  R1 = PHOTOCELL [package=photocell-kit]  # not connected

nets:
  N1: U1.VCC, U1.CH_PD
  N2: U1.GPIO_0, S2.Pin_3, S2.Pin_4
  N3: U1.GND, U1.GPIO_15, LED1.cathode, S2.Pin_1, S2.Pin_2, S1.Pin_1, S1.Pin_2
  N4: U1.GPIO_14, LED1.anode
  N5: U1.REST, S1.Pin_3, S1.Pin_4
  N6: IC1.OUT, U2.VCC

custom parts:
  4-Channel 5v Relay Shield: 4 Channel 5v Relay Shield w. 2x SPD-06VDC-SD-C
